# Fritzing sketch L298N_DC_Motor_single (saved by Fritzing 0.9.3b)

parts:
  S1 = H-Bridge with L298N
  부품1 = Arduino Uno (Rev3)
  BAT1 = BC9VPC [package=bc9vpc]
  M2 = DC Motor  # not connected

nets:
  N1: S1.12V, BAT1.V+
  GND: S1.GND, 부품1.GND, BAT1.V-
  N2: S1.IN1, 부품1.D11_PWM/MOSI
  N3: S1.IN2, 부품1.D10_PWM/SS

custom parts:
  H-Bridge with L298N: h-bridge
